# Fritzing sketch light-mixer-encoders (saved by Fritzing 0.9.6b)
# 18650 Li-ion Battery: CC-BY Dr Kristofer Chan, King's College London/Remote-research.org
breadboards: 1

parts:
  Part2 = Adafruit Breadboard-Friendly NeoPixel [part_number="Adafruit #1312"]
  RE1 = KY-040 Rotary encoder [package="Breakout board"]
  RE2 = KY-040 Rotary encoder [package="Breakout board"]
  RE3 = KY-040 Rotary encoder [package="Breakout board"]
  Part6 = PowerBoost 500 Charger
  Part7 = Arduino Nano (Rev3.0) (ICSP)
  BAT1 = 18650 Li-ion Battery [package=battery-18650]
  Squix1 = OLED 0.96" 128x64 I2C SSD1306
  S1 = Toggle Switch [package=THT]

nets:
  N1: Part2.IN, Part7.D8
  VDD: Part2.VDD, Part6.5.0V, Part7.5V, Squix1.VCC
  GND: Part2.GND, RE1.GND, RE2.GND, RE3.GND, Part6.GND, Part7.GND, Squix1.GND
  N2: RE1.SW, Part7.D11/MOSI
  N3: RE1.DT, Part7.D3
  N4: RE1.CLK, Part7.D2
  N5: RE2.SW, Part7.D10
  N6: RE2.DT, Part7.D5
  N7: RE2.CLK, Part7.D4
  N8: RE3.SW, Part7.D9
  N9: RE3.DT, Part7.D7
  N10: RE3.CLK, Part7.D6
  N11: Part6.GND_BAT_IN, BAT1.-
  N12: Part6.VBAT_IN, S1.COM
  N13: Part7.A5, Squix1.SCL
  N14: Part7.A4, Squix1.SCA
  N15: BAT1.+, S1.L1

custom parts:
  Adafruit Breadboard-Friendly NeoPixel: This is the easiest way possible to add small, bright RGB pixels to your project. We took the same technology from our Flora NeoPixels and made them breadboard friendly, with two rows of 3 x 0.1" spaced header on each side for easy soldering, chaining and breadboarding. These ultra-bright LEDs have a constant-current driver cooked right into the LED package! The pixels are chainable - so you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
  KY-040 Rotary encoder: KY-040 Rotary Encoder with switch on breakout borad from AZ Delivery
  18650 Li-ion Battery: 18650 li-ion Battery Standard 18650 battery with interactive connectors Creative Common Attribution 4.0 International (CC-BY 4.0) license. Any use of this part requires attribution of Dr Kristofer Chan, Department of Geography, King's College London. Contact kristofer.chan [at] kcl.ac.uk OR kris [at] remote-research.org for further information.
