# Fritzing sketch light-mixer (saved by Fritzing 0.9.6b)
breadboards: 1

parts:
  Part1 = Arduino Nano (Rev3.0)
  Part2 = Adafruit Breadboard-Friendly NeoPixel [part_number="Adafruit #1312"]
  R1 = Rotary Potentiometer (Large) [maximum_resistance=100kΩ package=THT]
  R2 = Rotary Potentiometer (Large) [maximum_resistance=100kΩ package=THT]
  R3 = Rotary Potentiometer (Large) [maximum_resistance=100kΩ package=THT]

nets:
  GND: Part1.GND, Part2.GND, R1.leg1, R2.leg1, R3.leg1
  N1: Part1.D3, Part2.IN
  5V: Part1.5V, Part2.VDD, R1.wiper, R2.wiper, R3.wiper
  N2: Part1.A3, R3.leg2
  N3: Part1.A2, R2.leg2
  N4: Part1.A1, R1.leg2

custom parts:
  Adafruit Breadboard-Friendly NeoPixel: This is the easiest way possible to add small, bright RGB pixels to your project. We took the same technology from our Flora NeoPixels and made them breadboard friendly, with two rows of 3 x 0.1" spaced header on each side for easy soldering, chaining and breadboarding. These ultra-bright LEDs have a constant-current driver cooked right into the LED package! The pixels are chainable - so you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
